// Logisim project 3주차과제_1_201921009_엄지호.circ as structural Verilog: 1 circuit, main circuit main
module main (
  input  X,
  input  Y,
  input  a,
  input  X_2,
  input  b,
  input  Y_2,
  input  c,
  input  d,
  output out_9,
  output out_10
);

  wire and_1_out, and_2_out, and_3_out, and_4_out, and_5_out, and_6_out, not_1_out, not_2_out, not_3_out,
       not_4_out, not_5_out, not_6_out, or_2_out, or_3_out, undriven, undriven_2;

  not not_1 (not_1_out, X);
  not not_2 (not_2_out, Y);
  and and_1 (and_1_out, not_1_out, Y);
  and and_2 (and_2_out, X, not_2_out);
  not not_3 (not_3_out, Y_2);
  not not_4 (not_4_out, X_2);
  not not_5 (not_5_out, Y_2);
  not not_6 (not_6_out, c);
  and and_3 (and_3_out, undriven, not_4_out, not_3_out);
  and and_4 (and_4_out, b, X_2, not_5_out);
  and and_5 (and_5_out, not_6_out, not_6_out, X_2, Y_2, Y_2);
  and and_6 (and_6_out, d, d, X_2, Y_2, undriven_2);
  or or_1 (out_9, and_1_out, and_2_out);
  or or_2 (or_2_out, and_3_out, and_4_out);
  or or_3 (or_3_out, and_5_out, and_6_out);
  or or_4 (out_10, or_2_out, or_3_out);
endmodule
