// Logisim project Dflipflop.circ as structural Verilog: 1 circuit, main circuit main
module main (
  input  D,
  input  CP,
  output D_2
);

  wire main_1_q, not_1_out, not_2_out;

  not not_1 (not_1_out, CP);
  Dlatch_main main_1 (.D(D), .CP(not_1_out), .Q(main_1_q));
  not not_2 (not_2_out, not_1_out);
  Dlatch_main main_2 (.D(main_1_q), .CP(not_2_out), .Q(D_2));
endmodule
